// Logisim project ex3.circ as structural Verilog: 2 circuits, main circuit rot1
module rot1 (
  input  [7:0] in_1,
  output [7:0] out_2
);


  assign out_2 = {in_1[0], in_1[7:1]};

  // Notes on the sheet:
  //   PUT CIRCUITRY HERE
endmodule

module Running_LED (
  input  [7:0] INITIAL_LED,
  input  RST,
  output [7:0] OUT_LED
);

  wire clock_1_out, not_1_out, or_1_out;
  wire [7:0] multiplexer_1_out, rot1_1_out_2;

  Clock clock_1 (.out(clock_1_out));
  not not_1 (not_1_out, RST);
  or or_1 (or_1_out, OUT_LED[0], OUT_LED[1], OUT_LED[2], OUT_LED[3], OUT_LED[5], OUT_LED[6], OUT_LED[7], OUT_LED[4]);
  LED led_1 (.in(OUT_LED[7]));
  Multiplexer #(.width(8), .enable("false")) multiplexer_1 (
    .in0(INITIAL_LED), .in1(OUT_LED), .out(multiplexer_1_out), .sel(not_1_out));
  LED led_2 (.in(OUT_LED[6]));
  Register register_1 (.D(rot1_1_out_2), .clk(clock_1_out), .Q(OUT_LED));  // open: en, clr
  rot1 rot1_1 (.in_1(multiplexer_1_out), .out_2(rot1_1_out_2));
  LED led_3 (.in(OUT_LED[5]));
  LED led_4 (.in(OUT_LED[4]));
  LED led_5 (.in(OUT_LED[3]));
  LED led_6 (.in(OUT_LED[2]));
  LED led_7 (.in(OUT_LED[1]));
  LED led_8 (.in(OUT_LED[0]));

  // Notes on the sheet:
  //   PUT CIRCUITS HERE
endmodule
