// Logisim project ex3_q3.circ as structural Verilog: 2 circuits, main circuit rot1
module rot1 (
  input  [7:0] in_1,
  output [7:0] out_2
);


  assign out_2 = {in_1[0], in_1[7:1]};

  // Notes on the sheet:
  //   PUT CIRCUITRY HERE
endmodule

module Running_LED (
  input  [7:0] INITIAL_LED,
  input  RST,
  output [7:0] OUT_LED
);

  wire [7:0] rot1_1_out_2, rot1_2_out_2, rot1_3_out_2, rot1_4_out_2, rot1_5_out_2, rot1_6_out_2, rot1_7_out_2;

  LED led_1 (.in(OUT_LED[7]));
  // Shift_Register shift_register_1: pin names not known
  rot1 rot1_1 (.in_1(INITIAL_LED), .out_2(rot1_1_out_2));
  LED led_2 (.in(OUT_LED[6]));
  ROM rom_1 ();  // open: addr, data
  rot1 rot1_2 (.in_1(rot1_3_out_2), .out_2(rot1_2_out_2));
  rot1 rot1_3 (.in_1(rot1_1_out_2), .out_2(rot1_3_out_2));
  LED led_3 (.in(OUT_LED[5]));
  rot1 rot1_4 (.in_1(rot1_2_out_2), .out_2(rot1_4_out_2));
  LED led_4 (.in(OUT_LED[4]));
  rot1 rot1_5 (.in_1(rot1_4_out_2), .out_2(rot1_5_out_2));
  rot1 rot1_6 (.in_1(rot1_5_out_2), .out_2(rot1_6_out_2));
  LED led_5 (.in(OUT_LED[3]));
  rot1 rot1_7 (.in_1(rot1_6_out_2), .out_2(rot1_7_out_2));
  LED led_6 (.in(OUT_LED[2]));
  rot1 rot1_8 (.in_1(rot1_7_out_2));  // open: out_2
  LED led_7 (.in(OUT_LED[1]));
  LED led_8 (.in(OUT_LED[0]));

  // Notes on the sheet:
  //   PUT CIRCUITS HERE
endmodule
